# Fritzing sketch Node (saved by Fritzing 0.8.7b)
breadboards: 1

parts:
  Part1 = Arduino Uno (Rev3) - ICSP
  J1 = double row male pin header, 10 pins [form="♂ (male)"]
  J2 = male pin header, 8 pins [form="♂ (male)"]
  U1 = RELAY-SOLIDSTATE [package=relay-s108t02]  # not connected

nets:
  GND: Part1.GND, J1.pin5, J2.pin6
  CS-ETHER: Part1.D8, J1.pin7
  RST: Part1.D9_PWM, J2.pin7
  CS-rfid: Part1.D10_PWM/SS, J2.pin1
  MISO: Part1.D11_PWM/MOSI, J1.pin2, J2.pin4
  MOSI: Part1.D12/MISO, J1.pin8, J2.pin3
  SCK: Part1.D13/SCK, J1.pin3, J2.pin2
  VCC: Part1.3V3, J1.pin6, J2.pin8
  INT: J1.pin1
  reset: J1.pin4
  WOL: J1.pin9
  CLKOUT: J1.pin10
  IRQ: J2.pin5
